// Logisim project XorLogic.circ as structural Verilog: 6 circuits, main circuit main
module main (
  input  in_1,
  input  in_2,
  input  in_3,
  output out_4,
  output out_5
);

  wire xor_1_out, xor_3_out, xor_4_out, xor_5_out, xor_6_out, xor_7_out, xor_9_out;

  xor xor_1 (xor_1_out, in_1, in_2);
  xor xor_2 (out_4, xor_1_out, in_3);
  xor xor_3 (xor_3_out, xor_1_out, 1'b1);
  xor xor_4 (xor_4_out, in_1, 1'b1);
  xor xor_5 (xor_5_out, in_3, xor_1_out);
  xor xor_6 (xor_6_out, in_2, in_1);
  ExactlyOne xor_7 (.out(xor_7_out), .in0(xor_3_out), .in1(1'b1), .in2(xor_5_out));
  xor xor_8 (out_5, xor_7_out, xor_9_out);
  ExactlyOne xor_9 (.out(xor_9_out), .in0(xor_4_out), .in1(1'b1), .in2(xor_6_out));
endmodule

module And (
  input  in_1,
  input  in_2,
  output out_3
);

  wire xor_1_out, xor_2_out;

  xor xor_1 (xor_1_out, in_1, 1'b1);
  xor xor_2 (xor_2_out, in_2, in_1);
  ExactlyOne xor_3 (.out(out_3), .in0(xor_1_out), .in1(1'b1), .in2(xor_2_out));
endmodule

module OR (
  input  in_1,
  input  in_2,
  output out_3
);

  wire xor_1_out, xor_2_out, xor_3_out, xor_4_out, xor_5_out;

  xor xor_1 (xor_1_out, in_1, in_2);
  xor xor_2 (xor_2_out, in_1, in_2);
  xor xor_3 (xor_3_out, xor_1_out, in_2);
  ExactlyOne xor_4 (.out(xor_4_out), .in0(xor_2_out), .in1(in_2), .in2(in_2));
  xor xor_5 (xor_5_out, xor_3_out, xor_1_out);
  xor xor_6 (out_3, xor_4_out, xor_5_out);
endmodule

module NOT (
  input  in_1,
  output out_2
);

  xor xor_1 (out_2, in_1, 1'b1);
endmodule

module Nand (
  input  in_1,
  input  in_2,
  output out_3
);

  wire xor_1_out, xor_2_out, xor_3_out;

  xor xor_1 (xor_1_out, in_1, 1'b1);
  xor xor_2 (xor_2_out, in_2, in_1);
  ExactlyOne xor_3 (.out(xor_3_out), .in0(xor_1_out), .in1(1'b1), .in2(xor_2_out));
  xor xor_4 (out_3, 1'b1, xor_3_out);
endmodule

module Nor (
  input  in_1,
  input  in_2,
  output out_3
);

  wire xor_1_out, xor_2_out, xor_3_out, xor_4_out, xor_5_out, xor_7_out;

  xor xor_1 (xor_1_out, in_1, in_2);
  xor xor_2 (xor_2_out, in_1, in_2);
  xor xor_3 (xor_3_out, xor_1_out, in_2);
  ExactlyOne xor_4 (.out(xor_4_out), .in0(xor_2_out), .in1(in_2), .in2(in_2));
  xor xor_5 (xor_5_out, xor_3_out, xor_1_out);
  xor xor_6 (out_3, 1'b1, xor_7_out);
  xor xor_7 (xor_7_out, xor_4_out, xor_5_out);
endmodule
